// Logisim project 4bit-cpu-architecture-light.circ as structural Verilog: 1 circuit, main circuit main
module main (
);

  wire ADD, adder_1_cout, CIN, CLK_out, COUTB, decoder_1_out0, decoder_1_out1, decoder_1_out2,
       decoder_1_out3, JMP, LOADEN, LOADPC, LOADRX, MOV, or_1_out, PCEN;
  wire [1:0] rom_1_data;
  wire [3:0] adder_1_out, multiplexer_1_out, multiplexer_2_out, O_q, PC_q, X_q, Y_q, Z_q;
  wire [5:2] rom_1_data_2;

  Decoder #(.select(2), .disabled(0)) decoder_1 (
    .out0(decoder_1_out0), .out1(decoder_1_out1), .out2(decoder_1_out2), .out3(decoder_1_out3),
    .sel(rom_1_data), .en(LOADEN));
  Clock CLK (.out(CLK_out));
  or or_1 (or_1_out, LOADRX, decoder_1_out0);
  Register #(.width(4)) X (.D(multiplexer_2_out), .en(or_1_out), .Q(X_q), .clk(CLK_out));  // open: clr
  Register #(.width(4)) Y (.D(multiplexer_2_out), .en(decoder_1_out1), .Q(Y_q), .clk(CLK_out));  // open: clr
  Register #(.width(4)) Z (.D(multiplexer_2_out), .en(decoder_1_out2), .Q(Z_q), .clk(CLK_out));  // open: clr
  Register #(.width(4)) O (.D(multiplexer_2_out), .en(decoder_1_out3), .Q(O_q), .clk(CLK_out));  // open: clr
  Counter #(.width(4), .max('hf)) PC (
    .load(LOADPC), .D(multiplexer_2_out), .count(PCEN), .Q(PC_q), .clk(CLK_out));  // open: carry, clr
  Hex_Digit_Display hex_digit_display_1 (.value(O_q));  // open: dp
  Adder #(.width(4)) adder_1 (.a(X_q), .b(Y_q), .out(adder_1_out), .cin(CIN), .cout(adder_1_cout));
  not not_1 (COUTB, adder_1_cout);
  Multiplexer #(.select(2), .width(4)) multiplexer_1 (
    .in0(X_q), .in1(Y_q), .in2(Z_q), .in3(O_q), .out(multiplexer_1_out), .sel(rom_1_data_2[3:2]));  // open: en
  ROM #(.addrWidth(4), .dataWidth(6)) rom_1 (
    .addr(PC_q), .data({rom_1_data_2[5], LOADEN, rom_1_data_2[3:2], rom_1_data}));  // open: sel
  Multiplexer #(.select(2), .width(4)) multiplexer_2 (
    .in0({rom_1_data_2[3:2], rom_1_data}), .in1(adder_1_out), .in2({rom_1_data_2[3:2], rom_1_data}),
    .in3(multiplexer_1_out), .out(multiplexer_2_out), .sel({rom_1_data_2[5], LOADEN}));  // open: en
  Decoder #(.select(2), .disabled(0)) decoder_2 (
    .out0(LOADRX), .out1(ADD), .out2(JMP), .out3(MOV), .sel({rom_1_data_2[5], LOADEN}));  // open: en
  nand nand_1 (PCEN, JMP, COUTB);
  and and_1 (CIN, ADD, rom_1_data_2[2]);
  not not_2 (LOADPC, PCEN);

  // Notes on the sheet:
  //   contents of rom_1 (hex, n*v repeats v):
  //   1 11 21 31 15 21
endmodule
